// Logisim project right-shift.circ as structural Verilog: 2 circuits, main circuit main
module main (
  input  [3:0] in,
  input  arithmetic,
  input  [1:0] shamt,
  output [3:0] out
);

  wire [3:0] multiplexer_1_out, right_shift_1_1_out, right_shift_1_2_out, right_shift_1_3_out;

  right_shift_1 right_shift_1_1 (.in(in), .arithmetic(arithmetic), .out(right_shift_1_1_out));
  Multiplexer #(.width(4), .enable("false")) multiplexer_1 (
    .in0(in), .in1(right_shift_1_1_out), .out(multiplexer_1_out), .sel(shamt[0]));
  right_shift_1 right_shift_1_2 (.in(right_shift_1_3_out), .arithmetic(arithmetic), .out(right_shift_1_2_out));
  right_shift_1 right_shift_1_3 (.in(multiplexer_1_out), .arithmetic(arithmetic), .out(right_shift_1_3_out));
  Multiplexer #(.width(4), .enable("false")) multiplexer_2 (
    .in0(multiplexer_1_out), .in1(right_shift_1_2_out), .out(out), .sel(shamt[1]));
endmodule

module right_shift_1 (
  input  [3:0] in,
  input  arithmetic,
  output [3:0] out
);


  assign out = {arithmetic, in[3:1]};
endmodule
