// Logisim project sample.circ as structural Verilog: 1 circuit, main circuit main
module main (
  input  A,
  input  B,
  input  C,
  output Z
);

  wire and_1_out, and_2_out, not_1_out, not_2_out, not_3_out, not_4_out;

  not not_1 (not_1_out, A);
  not not_2 (not_2_out, B);
  not not_3 (not_3_out, B);
  not not_4 (not_4_out, C);
  and and_1 (and_1_out, not_1_out, C, not_2_out);
  and and_2 (and_2_out, not_3_out, A, not_4_out);
  or or_1 (Z, and_1_out, B, and_2_out);

  // Notes on the sheet:
  //   Original expression: ~A~BC+~AB~C+~ABC+A~B~C+AB~C+ABC
  //   Simplified expression:  ~A~BC + A~B~C + B
endmodule
